# Fritzing sketch step-001 (saved by Fritzing 0.9.3b)
breadboards: 1

parts:
  LED1 = smd LED [color="Red (633nm)" package="0603 [SMD]"]
  R1 = Resistor [tolerance=±5% resistance=330 package=THT]
  PiZero1 = Raspberry Pi Zero

nets:
  N1: LED1.cathode, PiZero1.GPIO19
  N2: LED1.anode, R1.Pin_0
  N3: R1.Pin_1, PiZero1.GPIO4_(GCLK)
  N4: PiZero1.GPIO25_(GEN6), PiZero1.TV0

notes:
  GPIO13 (pin33)
  Gnd (pin6),
